# Fritzing sketch diagrama de conexiones (saved by Fritzing 0.9.3b)
breadboards: 1

parts:
  Arduino_Mega_2560 = Arduino Mega 2560 (Rev3)
  hc-sr1_(izquierda) = hc-sr04
  hc-sr2_(derecha) = hc-sr04
  L298N = L298N DC motor driver
  PortaBaterias = Battery
  Servo_MG996R = Basic Servo
  Motor = DC Motor

nets:
  N1: Arduino_Mega_2560.D8_PWM, Servo_MG996R.pulse
  VCC: Arduino_Mega_2560.5V, hc-sr1_(izquierda).VCC, hc-sr2_(derecha).VCC, Servo_MG996R.vcc
  GND: Arduino_Mega_2560.GND, hc-sr1_(izquierda).GND, hc-sr2_(derecha).GND, Servo_MG996R.gnd
  VIN: Arduino_Mega_2560.VIN, L298N.5V
  N2: Arduino_Mega_2560.D5_PWM, L298N.IN2
  N3: Arduino_Mega_2560.D6_PWM, L298N.IN1
  N4: Arduino_Mega_2560.D7_PWM, L298N.ENA
  N5: Arduino_Mega_2560.D50, hc-sr2_(derecha).Trig
  N6: Arduino_Mega_2560.D51, hc-sr2_(derecha).Echo
  N7: Arduino_Mega_2560.D52, hc-sr1_(izquierda).Trig
  N8: Arduino_Mega_2560.D53, hc-sr1_(izquierda).Echo
  N9: L298N.OUT1, Motor.pin_1
  N10: L298N.OUT2, Motor.pin_2
  N11: L298N.12V, PortaBaterias.+
  N12: L298N.GND, PortaBaterias.-

custom parts:
  L298N DC motor driver: 2x DC motor driver with 78M05 positive voltage regulator (7..35 V) L298N: max 46 V, 2 A Set 5 V Enable jumper to enable 5 V regultor (needed for the L298N) and +5 V output at screw terminal or supply external +5 V at screw terminal Set ENA and/or ENB to +5 V to enable motor permanently or supply ENA and/or ENB with PWM signal IN1 and IN2 set rotation directory for motor A (OUT1/OUT2) IN2 and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
